// Digital circuit Computing_Sistem.dig as structural Verilog
module Computing_Sistem (
);

  wire Instruction_Memory_q_0, Instruction_Memory_q_1, Instruction_Memory_q_2, Instruction_Memory_q_3,
       Instruction_Memory_q_4, Instruction_Memory_q_5, Instruction_Memory_q_6, Instruction_Memory_q_7,
       Instruction_Memory_q_8, Instruction_Memory_q_9, Instruction_Memory_q_10, Instruction_Memory_q_11,
       Instruction_Memory_q_12, Instruction_Memory_q_13, Instruction_Memory_q_14, Instruction_Memory_q_15,
       or_1_out, PC_p1, PC_p2, PC_p3, PC_p4, PC_p5, PC_p6, PC_p7, PC_p8, PC_p9, PC_p10, PC_p11, PC_p12,
       PC_p13, PC_p14, PC_p15, PC_p16, undriven, undriven_2, undriven_3, undriven_4;

  // Program_Counter PC: pin names not known; wires that end beside it: PC_p1, PC_p2, PC_p3, PC_p4, PC_p5, PC_p6, PC_p7, PC_p8, PC_p9, PC_p10, PC_p11, PC_p12, PC_p13, PC_p14, PC_p15, PC_p16
  or or_1 (or_1_out, undriven_4, undriven_3, undriven_2, undriven);
  _16_bit_IR Instruction_Memory (
    .D_0(PC_p1), .D_1(PC_p2), .D_2(PC_p3), .D_3(PC_p4), .D_4(PC_p5), .D_5(PC_p6), .D_6(PC_p7), .D_7(PC_p8),
    .D_8(PC_p9), .D_9(PC_p10), .D_10(PC_p11), .D_11(PC_p12), .D_12(PC_p13), .D_13(PC_p14), .D_14(PC_p15),
    .D_15(PC_p16), .Q_7(Instruction_Memory_q_7), .Q_6(Instruction_Memory_q_6), .Q_5(Instruction_Memory_q_5),
    .Q_4(Instruction_Memory_q_4), .Q_3(Instruction_Memory_q_3), .Q_0(Instruction_Memory_q_0),
    .Q_1(Instruction_Memory_q_1), .Q_2(Instruction_Memory_q_2), .Q_15(Instruction_Memory_q_15),
    .Q_14(Instruction_Memory_q_14), .Q_13(Instruction_Memory_q_13), .Q_12(Instruction_Memory_q_12),
    .Q_11(Instruction_Memory_q_11), .Q_8(Instruction_Memory_q_8), .Q_9(Instruction_Memory_q_9),
    .Q_10(Instruction_Memory_q_10));
  Semafor semafor_1 ();  // open: Enable_counters, Reset_counters, Async_counter1, Async_counter2, Async_counter3, Flag_sensor1, Flag_sensor2, Flag_sensor3, Emergency_sensor, Set_verde, Set_galben, Set_rosu, Begin, Q_0_0, Q_0_1, Q_0_2, Q_0_3, Q_0_4, Q_0_5, Q_0_6, Q_0_7, Q_1_0, Q_1_1, Q_1_2, Q_1_3, Q_1_4, Q_1_5, Q_1_6, Q_1_7, Q_2_0, Q_2_1, Q_2_2, Q_2_3, Q_2_4, Q_2_5, Q_2_6, Q_2_7, Flag_1, Flag_2, Flag_3, Emergency, Color_green, Color_yellow, Color_red
  Semafor semafor_2 ();  // open: Enable_counters, Reset_counters, Async_counter2, Async_counter3, Async_counter1, Flag_sensor1, Flag_sensor2, Flag_sensor3, Emergency_sensor, Set_verde, Set_galben, Set_rosu, Begin, Q_0_0, Q_0_1, Q_0_2, Q_0_3, Q_0_4, Q_0_5, Q_0_6, Q_0_7, Q_1_0, Q_1_1, Q_1_2, Q_1_3, Q_1_4, Q_1_5, Q_1_6, Q_1_7, Q_2_0, Q_2_1, Q_2_2, Q_2_3, Q_2_4, Q_2_5, Q_2_6, Q_2_7, Flag_1, Flag_2, Flag_3, Emergency, Color_green, Color_yellow, Color_red
  _8Registers_encoded _8registers_encoded_1 ();  // open: Select_input_0, Select_input_1, Select_input_2, Select_output_0, Select_output_1, Select_output_2, Input_0, Input_1, Input_2, Input_3, Input_4, Input_5, Input_6, Input_7, Input_8, Input_9, Input_10, Input_11, Input_12, Input_13, Input_14, Input_15, Clock, Reset, Output_0, Output_1, Output_2, Output_3, Output_4, Output_5, Output_6, Output_7, Output_8, Output_9, Output_10, Output_11, Output_12, Output_13, Output_14, Output_15
  Semafor semafor_3 ();  // open: Enable_counters, Reset_counters, Async_counter2, Async_counter3, Async_counter1, Flag_sensor1, Flag_sensor2, Flag_sensor3, Emergency_sensor, Set_verde, Set_galben, Set_rosu, Begin, Q_0_0, Q_0_1, Q_0_2, Q_0_3, Q_0_4, Q_0_5, Q_0_6, Q_0_7, Q_1_0, Q_1_1, Q_1_2, Q_1_3, Q_1_4, Q_1_5, Q_1_6, Q_1_7, Q_2_0, Q_2_1, Q_2_2, Q_2_3, Q_2_4, Q_2_5, Q_2_6, Q_2_7, Flag_1, Flag_2, Flag_3, Emergency, Color_green, Color_yellow, Color_red
  Semafor semafor_4 ();  // open: Enable_counters, Reset_counters, Async_counter2, Async_counter3, Async_counter1, Flag_sensor1, Flag_sensor2, Flag_sensor3, Emergency_sensor, Set_verde, Set_galben, Set_rosu, Begin, Q_0_0, Q_0_1, Q_0_2, Q_0_3, Q_0_4, Q_0_5, Q_0_6, Q_0_7, Q_1_0, Q_1_1, Q_1_2, Q_1_3, Q_1_4, Q_1_5, Q_1_6, Q_1_7, Q_2_0, Q_2_1, Q_2_2, Q_2_3, Q_2_4, Q_2_5, Q_2_6, Q_2_7, Flag_1, Flag_2, Flag_3, Emergency, Color_green, Color_yellow, Color_red

  // Notes on the sheet:
  //   exp
  //   CS bits
  //   BA bits
  //   CF bits
endmodule
